# Fritzing sketch Esquema - Raspberry com botão (saved by Fritzing 0.9.3b)
breadboards: 1

parts:
  S1 = Square Pushbutton
  S2 = Square Pushbutton
  Raspberry_Pi1 = Raspberry Pi B+
  D2F1 = D2F-FL Omron Snap Action Limit Switch with Level
  D2F2 = D2F-FL Omron Snap Action Limit Switch with Level
  D2F3 = D2F-FL Omron Snap Action Limit Switch with Level
  D2F4 = D2F-FL Omron Snap Action Limit Switch with Level
  D2F5 = D2F-FL Omron Snap Action Limit Switch with Level
  D2F6 = D2F-FL Omron Snap Action Limit Switch with Level

nets:
  N1: S1.leg0, S2.leg0, Raspberry_Pi1.GND, D2F1.COM, D2F2.COM, D2F3.COM, D2F4.COM, D2F5.COM, D2F6.COM
  N2: S1.leg1, Raspberry_Pi1.GPIO4
  N3: S2.leg1, Raspberry_Pi1.GPIO25
  N4: Raspberry_Pi1.GPIO17, D2F6.NO
  N5: Raspberry_Pi1.GPIO27, D2F4.NO
  N6: Raspberry_Pi1.GPIO22, D2F3.NO
  N7: Raspberry_Pi1.GPIO24, D2F1.NO
  N8: Raspberry_Pi1.GPIO23, D2F2.NO
  N9: Raspberry_Pi1.GPIO18, D2F5.NO

custom parts:
  D2F-FL Omron Snap Action Limit Switch with Level: Snap action switch with stainless steel lever.
